# Fritzing sketch circuit (saved by Fritzing 0.9.3b)
breadboards: 1

parts:
  U1 = NodeMCU V1.0
  LED1 = LED - 3mm [color="Red (633nm)" package="3 mm [THT]"]
  DHT1 = DHT11 Humitidy and Temperature Sensor
  LED2 = LED - 3mm [color="Red (633nm)" package="3 mm [THT]"]
  J1 = Piezo Speaker
  Mod1 = KY-026 Flame Sensor Module [package="Breakout board"]

nets:
  N1: U1.D0, LED2.anode
  N2: U1.D1, Mod1.D0
  N3: U1.D2, LED1.cathode
  N4: U1.D3, DHT1.DATA
  N5: U1.GND, LED1.anode, DHT1.NULL
  N6: U1.D5, J1.pin2
  N7: U1.TX, DHT1.GND, LED2.cathode, J1.pin1, Mod1.G, Mod1.+

custom parts:
  NodeMCU V1.0: ESP8266 based NodeMCU
  DHT11 Humitidy and Temperature Sensor: DHT11 Humidity and Temperature Sensor
  KY-026 Flame Sensor Module: KY-026 Flame Sensor Module reacts in the presence of fire.
